// Logisim project proj1.circ as structural Verilog: 7 circuits, main circuit 3:2 Adder
module _3_2_Adder (
  input  CarryIn,
  input  A,
  input  B,
  output CarryOut,
  output Sum
);

  wire and_1_out, and_2_out, and_3_out, and_4_out, and_5_out, and_6_out, and_7_out, not_1_out, not_2_out,
       not_3_out;

  not not_1 (not_1_out, A);
  not not_2 (not_2_out, B);
  not not_3 (not_3_out, CarryIn);
  and and_1 (and_1_out, A, CarryIn);
  and and_2 (and_2_out, B, CarryIn);
  and and_3 (and_3_out, A, B);
  and and_4 (and_4_out, not_1_out, not_2_out, CarryIn);
  and and_5 (and_5_out, not_1_out, B, not_3_out);
  and and_6 (and_6_out, A, not_2_out, not_3_out);
  and and_7 (and_7_out, A, B, CarryIn);
  or or_1 (CarryOut, and_1_out, and_2_out, and_3_out);
  or or_2 (Sum, and_4_out, and_5_out, and_6_out, and_7_out);
endmodule

module _4_bit_Ripple_Adder (
  input  CarryIn,
  input  [3:0] A,
  input  [3:0] B,
  output [3:0] Sum,
  output CarryOut
);

  wire n3_2_adder_1_carryout, n3_2_adder_2_carryout, n3_2_adder_3_carryout;

  _3_2_Adder u_3_2_adder_1 (.A(A[0]), .B(B[0]), .CarryIn(CarryIn), .CarryOut(n3_2_adder_1_carryout), .Sum(Sum[0]));
  _3_2_Adder u_3_2_adder_2 (
    .A(A[1]), .B(B[1]), .CarryIn(n3_2_adder_1_carryout), .CarryOut(n3_2_adder_2_carryout), .Sum(Sum[1]));
  _3_2_Adder u_3_2_adder_3 (
    .A(A[2]), .B(B[2]), .CarryIn(n3_2_adder_2_carryout), .CarryOut(n3_2_adder_3_carryout), .Sum(Sum[2]));
  _3_2_Adder u_3_2_adder_4 (.A(A[3]), .B(B[3]), .CarryIn(n3_2_adder_3_carryout), .CarryOut(CarryOut), .Sum(Sum[3]));
endmodule

module _4_bit_counter (
  input  Increment,
  input  Reset,
  input  Clock,
  output [3:0] Output
);

  wire [3:0] bit_extender_1_out, n4_bit_ripple_adder_1_sum;

  assign bit_extender_1_out = {{3{1'b0}}, Increment};  // Bit_Extender bit_extender_1
  _4_bit_Ripple_Adder u_4_bit_ripple_adder_1 (
    .A(bit_extender_1_out), .B(Output), .CarryIn(1'b0), .Sum(n4_bit_ripple_adder_1_sum));  // open: CarryOut
  Register #(.width(4)) register_1 (.D(n4_bit_ripple_adder_1_sum), .Q(Output), .clk(Clock), .clr(Reset));  // open: en
endmodule

module left_player (
  input  A,
  input  B,
  input  C,
  input  D,
  input  Go,
  input  Clock,
  input  Reset,
  output Win_Tie,
  output [3:0] Score
);

  wire and_1_out, and_2_out, and_3_out, and_4_out, and_5_out, and_6_out, and_7_out, and_8_out, and_9_out,
       and_10_out, and_11_out, and_12_out, and_13_out, not_1_out, not_2_out, not_3_out, not_4_out, or_2_out;

  and and_1 (and_1_out, A, Go);
  and and_2 (and_2_out, B, Go);
  and and_3 (and_3_out, C, Go);
  and and_4 (and_4_out, D, D, Go);
  not not_1 (not_1_out, and_1_out);
  not not_2 (not_2_out, and_2_out);
  not not_3 (not_3_out, and_3_out);
  not not_4 (not_4_out, and_4_out);
  and and_5 (and_5_out, not_1_out, not_2_out, not_3_out, not_4_out);
  and and_6 (and_6_out, not_1_out, not_2_out, and_3_out, and_4_out);
  and and_7 (and_7_out, and_1_out, and_2_out, and_3_out, and_4_out);
  and and_8 (and_8_out, and_1_out, and_2_out, and_3_out, not_4_out);
  and and_9 (and_9_out, and_1_out, not_2_out, not_3_out, not_4_out);
  and and_10 (and_10_out, and_1_out, not_2_out, and_3_out, not_4_out);
  and and_11 (and_11_out, not_1_out, not_2_out, and_3_out, and_4_out);
  and and_12 (and_12_out, and_1_out, and_2_out, and_3_out, not_4_out);
  and and_13 (and_13_out, and_1_out, not_2_out, not_3_out, not_4_out);
  or or_1 (Win_Tie, and_5_out, and_6_out, and_6_out, and_7_out, and_8_out, and_9_out, and_10_out);
  or or_2 (or_2_out, and_11_out, and_12_out, and_13_out);
  _4_bit_counter u_4_bit_counter_1 (.Increment(or_2_out), .Reset(Reset), .Clock(Clock), .Output(Score));

  // Notes on the sheet:
  //   for evaluating, use 4 and gates with each input; a*go, b*go etc
endmodule

module right_player (
  input  A,
  input  B,
  input  C,
  input  D,
  input  Go,
  input  Reset,
  input  Clock,
  output Win_Tie,
  output [3:0] Score
);

  wire and_1_out, and_2_out, and_3_out, and_4_out, and_5_out, and_6_out, and_7_out, and_8_out, and_9_out,
       and_10_out, and_11_out, and_12_out, and_13_out, or_2_out;

  and and_1 (and_1_out, A, Go);
  and and_2 (and_2_out, B, Go);
  and and_3 (and_3_out, C, Go);
  and and_4 (and_4_out, D, Go);
  and and_5 (and_5_out, ~and_1_out, ~and_2_out, ~and_3_out, ~and_4_out);  // AND_Gate
  and and_6 (and_6_out, ~and_1_out, ~and_2_out, and_3_out, ~and_4_out);  // AND_Gate
  and and_7 (and_7_out, and_1_out, and_2_out, ~and_3_out, ~and_4_out);  // AND_Gate
  and and_8 (and_8_out, and_1_out, and_2_out, and_3_out, and_4_out);
  and and_9 (and_9_out, and_1_out, ~and_2_out, and_3_out, and_4_out);  // AND_Gate
  and and_10 (and_10_out, and_1_out, ~and_2_out, and_3_out, ~and_4_out);  // AND_Gate
  and and_11 (and_11_out, ~and_1_out, ~and_2_out, and_3_out, ~and_4_out);  // AND_Gate
  and and_12 (and_12_out, and_1_out, and_2_out, ~and_3_out, ~and_4_out);  // AND_Gate
  and and_13 (and_13_out, and_1_out, ~and_2_out, and_3_out, and_4_out);  // AND_Gate
  or or_1 (Win_Tie, and_5_out, and_6_out, and_7_out, and_8_out, and_9_out, and_10_out);
  or or_2 (or_2_out, and_11_out, and_12_out, and_13_out);
  _4_bit_counter u_4_bit_counter_1 (.Increment(or_2_out), .Reset(Reset), .Clock(Clock), .Output(Score));
endmodule

module main (
  input  A,
  input  B,
  input  C,
  input  D,
  input  Reset,
  input  Go
);

  wire Clock_out, left_player_1_win_tie, right_player_1_win_tie;
  wire [3:0] left_player_1_score, right_player_1_score;

  Hex_Digit_Display hex_digit_display_1 (.value(left_player_1_score));  // open: dp
  left_player left_player_1 (
    .A(A), .B(B), .C(C), .D(D), .Go(Go), .Clock(Clock_out), .Reset(Reset), .Win_Tie(left_player_1_win_tie),
    .Score(left_player_1_score));
  LED Left_Win_Tie (.in(left_player_1_win_tie));
  right_player right_player_1 (
    .A(A), .B(B), .C(C), .D(D), .Go(Go), .Reset(Reset), .Clock(Clock_out), .Win_Tie(right_player_1_win_tie),
    .Score(right_player_1_score));
  Hex_Digit_Display hex_digit_display_2 (.value(right_player_1_score));  // open: dp
  LED Right_Win_Tie (.in(right_player_1_win_tie));
  Clock Clock (.out(Clock_out));

  // Notes on the sheet:
  //   Austin Bailey, Project 1
  //   Left Player
  //   Left Score
  //   Right Player
  //   Right Score
endmodule

module _16_bit_ALU (
  input  [15:0] A,
  input  [15:0] B,
  input  [4:0] Operations,
  output [15:0] Result
);

  wire n4_bit_ripple_adder_1_carryout, n4_bit_ripple_adder_2_carryout, n4_bit_ripple_adder_3_carryout,
       n4_bit_ripple_adder_5_carryout, n4_bit_ripple_adder_6_carryout, n4_bit_ripple_adder_7_carryout;
  wire [3:0] n4_bit_ripple_adder_1_sum, n4_bit_ripple_adder_2_sum, n4_bit_ripple_adder_3_sum,
       n4_bit_ripple_adder_4_sum, n4_bit_ripple_adder_5_sum, n4_bit_ripple_adder_6_sum,
       n4_bit_ripple_adder_7_sum, n4_bit_ripple_adder_8_sum, not_1_out, not_2_out, not_3_out, not_4_out;
  wire [15:0] and_1_out, or_1_out;

  assign not_1_out = ~B[7:4];  // NOT_Gate not_1, 4 bits wide
  assign not_2_out = ~B[3:0];  // NOT_Gate not_2, 4 bits wide
  assign not_3_out = ~B[11:8];  // NOT_Gate not_3, 4 bits wide
  assign not_4_out = ~B[15:12];  // NOT_Gate not_4, 4 bits wide
  _4_bit_Ripple_Adder u_4_bit_ripple_adder_1 (
    .A(A[3:0]), .B(B[3:0]), .CarryIn(1'b0), .CarryOut(n4_bit_ripple_adder_1_carryout),
    .Sum(n4_bit_ripple_adder_1_sum));
  _4_bit_Ripple_Adder u_4_bit_ripple_adder_2 (
    .A(A[7:4]), .B(B[7:4]), .CarryIn(n4_bit_ripple_adder_1_carryout),
    .CarryOut(n4_bit_ripple_adder_2_carryout), .Sum(n4_bit_ripple_adder_2_sum));
  _4_bit_Ripple_Adder u_4_bit_ripple_adder_3 (
    .A(A[11:8]), .B(B[11:8]), .CarryIn(n4_bit_ripple_adder_2_carryout),
    .CarryOut(n4_bit_ripple_adder_3_carryout), .Sum(n4_bit_ripple_adder_3_sum));
  _4_bit_Ripple_Adder u_4_bit_ripple_adder_4 (
    .A(A[15:12]), .B(B[15:12]), .CarryIn(n4_bit_ripple_adder_3_carryout), .Sum(n4_bit_ripple_adder_4_sum));  // open: CarryOut
  assign and_1_out = A & B;  // AND_Gate and_1, 16 bits wide
  assign or_1_out = A | B;  // OR_Gate or_1, 16 bits wide
  _4_bit_Ripple_Adder u_4_bit_ripple_adder_5 (
    .A(A[3:0]), .B(not_2_out), .CarryIn(1'b1), .CarryOut(n4_bit_ripple_adder_5_carryout),
    .Sum(n4_bit_ripple_adder_5_sum));
  _4_bit_Ripple_Adder u_4_bit_ripple_adder_6 (
    .A(A[7:4]), .B(not_1_out), .CarryIn(n4_bit_ripple_adder_5_carryout),
    .CarryOut(n4_bit_ripple_adder_6_carryout), .Sum(n4_bit_ripple_adder_6_sum));
  _4_bit_Ripple_Adder u_4_bit_ripple_adder_7 (
    .A(A[11:8]), .B(not_3_out), .CarryIn(n4_bit_ripple_adder_6_carryout),
    .CarryOut(n4_bit_ripple_adder_7_carryout), .Sum(n4_bit_ripple_adder_7_sum));
  _4_bit_Ripple_Adder u_4_bit_ripple_adder_8 (
    .A(A[15:12]), .B(not_4_out), .CarryIn(n4_bit_ripple_adder_7_carryout), .Sum(n4_bit_ripple_adder_8_sum));  // open: CarryOut
  Multiplexer #(.select(5), .width(16)) multiplexer_1 (
    .in0(or_1_out),
    .in1({n4_bit_ripple_adder_4_sum, n4_bit_ripple_adder_3_sum, n4_bit_ripple_adder_2_sum, n4_bit_ripple_adder_1_sum}),
    .in2(and_1_out),
    .in3({n4_bit_ripple_adder_4_sum, n4_bit_ripple_adder_3_sum, n4_bit_ripple_adder_2_sum, n4_bit_ripple_adder_1_sum}),
    .in5({n4_bit_ripple_adder_8_sum, n4_bit_ripple_adder_7_sum, n4_bit_ripple_adder_6_sum, n4_bit_ripple_adder_5_sum}),
    .in7({n4_bit_ripple_adder_4_sum, n4_bit_ripple_adder_3_sum, n4_bit_ripple_adder_2_sum, n4_bit_ripple_adder_1_sum}),
    .in9({n4_bit_ripple_adder_4_sum, n4_bit_ripple_adder_3_sum, n4_bit_ripple_adder_2_sum, n4_bit_ripple_adder_1_sum}),
    .in11({n4_bit_ripple_adder_4_sum, n4_bit_ripple_adder_3_sum, n4_bit_ripple_adder_2_sum, n4_bit_ripple_adder_1_sum}),
    .in15({n4_bit_ripple_adder_4_sum, n4_bit_ripple_adder_3_sum, n4_bit_ripple_adder_2_sum, n4_bit_ripple_adder_1_sum}),
    .in16(or_1_out),
    .in17({n4_bit_ripple_adder_4_sum, n4_bit_ripple_adder_3_sum, n4_bit_ripple_adder_2_sum, n4_bit_ripple_adder_1_sum}),
    .in18(and_1_out),
    .in21({n4_bit_ripple_adder_8_sum, n4_bit_ripple_adder_7_sum, n4_bit_ripple_adder_6_sum, n4_bit_ripple_adder_5_sum}),
    .in23({n4_bit_ripple_adder_4_sum, n4_bit_ripple_adder_3_sum, n4_bit_ripple_adder_2_sum, n4_bit_ripple_adder_1_sum}),
    .out(Result), .sel(Operations));  // open: in4, in6, in8, in10, in12, in13, in14, in19, in20, in22, in24, in25, in26, in27, in28, in29, in30, in31, en

  // Notes on the sheet:
  //   split into 4 parts (4 bits) for each part for A and B
  //   for overflow, connect all the 4 bit ripple adders
  //   subtraction has to do with signed 2 complements
  //   route logic by splitting operations into 5 bits and look at bit patterns
endmodule
