// Logisim project proj2.circ as structural Verilog: 8 circuits, main circuit 3:2 Adder
module Main (
  input  [2:0] RegA,
  input  [2:0] RegB,
  input  [2:0] RegW,
  input  WWrite,
  input  [4:0] ALUOp,
  input  [15:0] WIn,
  input  CondUpdate,
  input  Reset,
  input  [2:0] BranchType,
  output Z,
  output C,
  output N,
  output V,
  output [15:0] WOut,
  output [15:0] ALUOut,
  output [15:0] PC,
  output PCSel
);

  wire Clock_out, not_1_out, not_2_out, not_3_out;
  wire [3:0] n16_bit_alu_1_condition_codes;
  wire [15:0] Inst, NextPC, PC_q, register_file_1_a_bus, register_file_1_w_bus;

  Clock Clock (.out(Clock_out));
  not not_1 (not_1_out, Clock_out);
  Branch_Control_Unit branch_control_unit_1 (.BranchType(BranchType), .CondCodes({V, N, C, Z}), .PCSel(PCSel));
  Register_File register_file_1 (
    .WData(WIn), .Reset(Reset), .Clock(not_1_out), .WEn(WWrite), .ASel(RegA), .BSel(RegB), .WSel(RegW),
    .A_Bus(register_file_1_a_bus), .B_Bus(WOut), .W_Bus(register_file_1_w_bus));
  _16_bit_counter u_16_bit_counter_1 (.Clock(Clock_out), .Reset(Reset), .NextPC(NextPC));
  _16_bit_ALU u_16_bit_alu_1 (
    .A(register_file_1_a_bus), .B(register_file_1_w_bus), .Result(ALUOut),
    .Condition_Codes(n16_bit_alu_1_condition_codes), .Operations(ALUOp));
  not not_2 (not_2_out, Clock_out);
  Register #(.width(4)) CondCodes (
    .D(n16_bit_alu_1_condition_codes), .en(CondUpdate), .Q({V, N, C, Z}), .clk(not_2_out), .clr(Reset));
  Register #(.width(16)) u_PC (.D(NextPC), .Q(PC_q), .clk(not_3_out), .clr(Reset));  // open: en
  not not_3 (not_3_out, Clock_out);
  Register #(.width(16)) Current_PC (.D(PC_q), .Q(PC), .clk(Clock_out), .clr(Reset));  // open: en
  RAM #(.addrWidth(16), .dataWidth(16), .bus("asynch")) ram_1 (.addr(PC_q), .data(Inst), .clr(Reset));  // open: sel, ld
  Register #(.width(16)) IR (.D(Inst), .clk(Clock_out), .clr(Reset));  // open: en, Q

  // Other names for the same wires on the sheet: CondCodes[3:0] = {V, N, C, Z}

  // Notes on the sheet:
  //   Austin Bailey
  //   HW4
  //   add 65 to each worst case for hw3.c
  //   polygon tool to make ALU look closer
  //   Use an adder to correctly increment PC.
endmodule

module _3_2_Adder (
  input  CarryIn,
  input  A,
  input  B,
  output CarryOut,
  output Sum
);

  wire and_1_out, and_2_out, and_3_out, and_4_out, and_5_out, and_6_out, and_7_out, not_1_out, not_2_out,
       not_3_out;

  not not_1 (not_1_out, A);
  not not_2 (not_2_out, B);
  not not_3 (not_3_out, CarryIn);
  and and_1 (and_1_out, A, CarryIn);
  and and_2 (and_2_out, B, CarryIn);
  and and_3 (and_3_out, A, B);
  and and_4 (and_4_out, not_1_out, not_2_out, CarryIn);
  and and_5 (and_5_out, not_1_out, B, not_3_out);
  and and_6 (and_6_out, A, not_2_out, not_3_out);
  and and_7 (and_7_out, A, B, CarryIn);
  or or_1 (CarryOut, and_1_out, and_2_out, and_3_out);
  or or_2 (Sum, and_4_out, and_5_out, and_6_out, and_7_out);
endmodule

module _4_bit_Ripple_Adder (
  input  CarryIn,
  input  [3:0] A,
  input  [3:0] B,
  output [3:0] Sum,
  output CarryOut
);

  wire n3_2_adder_1_carryout, n3_2_adder_2_carryout, n3_2_adder_3_carryout;

  _3_2_Adder u_3_2_adder_1 (.A(A[0]), .B(B[0]), .CarryIn(CarryIn), .CarryOut(n3_2_adder_1_carryout), .Sum(Sum[0]));
  _3_2_Adder u_3_2_adder_2 (
    .A(A[1]), .B(B[1]), .CarryIn(n3_2_adder_1_carryout), .CarryOut(n3_2_adder_2_carryout), .Sum(Sum[1]));
  _3_2_Adder u_3_2_adder_3 (
    .A(A[2]), .B(B[2]), .CarryIn(n3_2_adder_2_carryout), .CarryOut(n3_2_adder_3_carryout), .Sum(Sum[2]));
  _3_2_Adder u_3_2_adder_4 (.A(A[3]), .B(B[3]), .CarryIn(n3_2_adder_3_carryout), .CarryOut(CarryOut), .Sum(Sum[3]));
endmodule

module _16_bit_ALU (
  input  [15:0] A,
  input  [15:0] B,
  input  [4:0] Operations,
  output [15:0] Result,
  output [3:0] Condition_Codes
);

  wire and_2_out, and_3_out, n4_bit_ripple_adder_1_carryout, n4_bit_ripple_adder_2_carryout,
       n4_bit_ripple_adder_3_carryout, n4_bit_ripple_adder_4_carryout, n4_bit_ripple_adder_5_carryout,
       n4_bit_ripple_adder_6_carryout, n4_bit_ripple_adder_7_carryout, n4_bit_ripple_adder_8_carryout;
  wire [3:0] n4_bit_ripple_adder_1_sum, n4_bit_ripple_adder_2_sum, n4_bit_ripple_adder_3_sum,
       n4_bit_ripple_adder_4_sum, n4_bit_ripple_adder_5_sum, n4_bit_ripple_adder_6_sum,
       n4_bit_ripple_adder_7_sum, n4_bit_ripple_adder_8_sum, not_1_out, not_2_out, not_3_out, not_4_out;
  wire [15:0] and_1_out, not_5_out, or_1_out, Z_out;

  assign not_1_out = ~B[7:4];  // NOT_Gate not_1, 4 bits wide
  assign not_2_out = ~B[3:0];  // NOT_Gate not_2, 4 bits wide
  assign not_3_out = ~B[11:8];  // NOT_Gate not_3, 4 bits wide
  assign not_4_out = ~B[15:12];  // NOT_Gate not_4, 4 bits wide
  _4_bit_Ripple_Adder u_4_bit_ripple_adder_1 (
    .A(A[3:0]), .B(B[3:0]), .CarryIn(1'b0), .CarryOut(n4_bit_ripple_adder_1_carryout),
    .Sum(n4_bit_ripple_adder_1_sum));
  _4_bit_Ripple_Adder u_4_bit_ripple_adder_2 (
    .A(A[7:4]), .B(B[7:4]), .CarryIn(n4_bit_ripple_adder_1_carryout),
    .CarryOut(n4_bit_ripple_adder_2_carryout), .Sum(n4_bit_ripple_adder_2_sum));
  _4_bit_Ripple_Adder u_4_bit_ripple_adder_3 (
    .A(A[11:8]), .B(B[11:8]), .CarryIn(n4_bit_ripple_adder_2_carryout),
    .CarryOut(n4_bit_ripple_adder_3_carryout), .Sum(n4_bit_ripple_adder_3_sum));
  _4_bit_Ripple_Adder u_4_bit_ripple_adder_4 (
    .A(A[15:12]), .B(B[15:12]), .CarryIn(n4_bit_ripple_adder_3_carryout),
    .CarryOut(n4_bit_ripple_adder_4_carryout), .Sum(n4_bit_ripple_adder_4_sum));
  assign and_1_out = A & B;  // AND_Gate and_1, 16 bits wide
  assign or_1_out = A | B;  // OR_Gate or_1, 16 bits wide
  _4_bit_Ripple_Adder u_4_bit_ripple_adder_5 (
    .A(A[3:0]), .B(not_2_out), .CarryIn(1'b1), .CarryOut(n4_bit_ripple_adder_5_carryout),
    .Sum(n4_bit_ripple_adder_5_sum));
  _4_bit_Ripple_Adder u_4_bit_ripple_adder_6 (
    .A(A[7:4]), .B(not_1_out), .CarryIn(n4_bit_ripple_adder_5_carryout),
    .CarryOut(n4_bit_ripple_adder_6_carryout), .Sum(n4_bit_ripple_adder_6_sum));
  _4_bit_Ripple_Adder u_4_bit_ripple_adder_7 (
    .A(A[11:8]), .B(not_3_out), .CarryIn(n4_bit_ripple_adder_6_carryout),
    .CarryOut(n4_bit_ripple_adder_7_carryout), .Sum(n4_bit_ripple_adder_7_sum));
  _4_bit_Ripple_Adder u_4_bit_ripple_adder_8 (
    .A(A[15:12]), .B(not_4_out), .CarryIn(n4_bit_ripple_adder_7_carryout),
    .CarryOut(n4_bit_ripple_adder_8_carryout), .Sum(n4_bit_ripple_adder_8_sum));
  Multiplexer #(.select(5), .width(16)) multiplexer_1 (
    .in0(or_1_out),
    .in1({n4_bit_ripple_adder_4_sum, n4_bit_ripple_adder_3_sum, n4_bit_ripple_adder_2_sum, n4_bit_ripple_adder_1_sum}),
    .in2(and_1_out),
    .in3({n4_bit_ripple_adder_4_sum, n4_bit_ripple_adder_3_sum, n4_bit_ripple_adder_2_sum, n4_bit_ripple_adder_1_sum}),
    .in5({n4_bit_ripple_adder_8_sum, n4_bit_ripple_adder_7_sum, n4_bit_ripple_adder_6_sum, n4_bit_ripple_adder_5_sum}),
    .in7({n4_bit_ripple_adder_4_sum, n4_bit_ripple_adder_3_sum, n4_bit_ripple_adder_2_sum, n4_bit_ripple_adder_1_sum}),
    .in9({n4_bit_ripple_adder_4_sum, n4_bit_ripple_adder_3_sum, n4_bit_ripple_adder_2_sum, n4_bit_ripple_adder_1_sum}),
    .in11({n4_bit_ripple_adder_4_sum, n4_bit_ripple_adder_3_sum, n4_bit_ripple_adder_2_sum, n4_bit_ripple_adder_1_sum}),
    .in15({n4_bit_ripple_adder_4_sum, n4_bit_ripple_adder_3_sum, n4_bit_ripple_adder_2_sum, n4_bit_ripple_adder_1_sum}),
    .in16(or_1_out),
    .in17({n4_bit_ripple_adder_4_sum, n4_bit_ripple_adder_3_sum, n4_bit_ripple_adder_2_sum, n4_bit_ripple_adder_1_sum}),
    .in18(and_1_out),
    .in21({n4_bit_ripple_adder_8_sum, n4_bit_ripple_adder_7_sum, n4_bit_ripple_adder_6_sum, n4_bit_ripple_adder_5_sum}),
    .in23({n4_bit_ripple_adder_4_sum, n4_bit_ripple_adder_3_sum, n4_bit_ripple_adder_2_sum, n4_bit_ripple_adder_1_sum}),
    .out(Result), .sel(Operations));  // open: in4, in6, in8, in10, in12, in13, in14, in19, in20, in22, in24, in25, in26, in27, in28, in29, in30, in31, en
  assign Z_out = Result | {16{1'b0}};  // OR_Gate Z, 16 bits wide
  and N (Condition_Codes[2], Result[15], 1'b1);
  assign not_5_out = ~Z_out;  // NOT_Gate not_5, 16 bits wide
  and and_2 (and_2_out, Result[15], ~B[15], ~A[15]);  // AND_Gate
  or V (Condition_Codes[3], and_2_out, and_3_out);
  and and_3 (and_3_out, ~Result[15], A[15], A[15]);  // AND_Gate
  and C (Condition_Codes[1], n4_bit_ripple_adder_4_carryout, n4_bit_ripple_adder_8_carryout);
  and and_4 (Condition_Codes[0], not_5_out[0], not_5_out[1], not_5_out[2], not_5_out[3], not_5_out[4], not_5_out[5], not_5_out[6], not_5_out[7], not_5_out[9], not_5_out[10], not_5_out[11], not_5_out[12], not_5_out[8], not_5_out[14], not_5_out[15], not_5_out[13]);

  // Notes on the sheet:
  //   split into 4 parts (4 bits) for each part for A and B
  //   for overflow, connect all the 4 bit ripple adders
  //   subtraction has to do with signed 2 complements
  //   route logic by splitting operations into 5 bits and look at bit patterns
endmodule

module Register_File (
  input  [15:0] WData,
  input  Reset,
  input  Clock,
  input  WEn,
  input  [2:0] ASel,
  input  [2:0] BSel,
  input  [2:0] WSel,
  output [15:0] A_Bus,
  output [15:0] B_Bus,
  output [15:0] W_Bus
);

  wire and_1_out, and_2_out, and_3_out, and_4_out, and_5_out, and_6_out, and_7_out, and_8_out, and_9_out,
       and_10_out, and_11_out, and_12_out, and_13_out, and_14_out, and_15_out, and_16_out, and_17_out;
  wire [15:0] register_1_q, register_2_q, register_3_q, register_4_q, register_5_q, register_6_q,
       register_7_q, register_8_q;

  and and_1 (and_1_out, ~WSel[0], ~WSel[1], ~WSel[2]);  // AND_Gate
  and and_2 (and_2_out, WSel[0], ~WSel[1], ~WSel[2]);  // AND_Gate
  and and_3 (and_3_out, ~WSel[0], WSel[1], ~WSel[2]);  // AND_Gate
  and and_4 (and_4_out, WSel[0], WSel[1], ~WSel[2]);  // AND_Gate
  and and_5 (and_5_out, ~WSel[0], ~WSel[1], WSel[2]);  // AND_Gate
  and and_6 (and_6_out, WSel[0], ~WSel[1], WSel[2]);  // AND_Gate
  and and_7 (and_7_out, ~WSel[0], WSel[1], WSel[2]);  // AND_Gate
  and and_8 (and_8_out, WSel[0], WSel[1], WSel[2]);
  and and_9 (and_9_out, and_1_out, WEn);
  and and_10 (and_10_out, and_2_out, WEn);
  and and_11 (and_11_out, and_3_out, WEn);
  and and_12 (and_12_out, and_4_out, WEn);
  and and_13 (and_13_out, and_5_out, WEn);
  and and_14 (and_14_out, and_6_out, WEn);
  and and_15 (and_15_out, and_7_out, WEn);
  and and_16 (and_16_out, and_8_out, WEn);
  and and_17 (and_17_out, Clock, WEn);
  Register #(.width(16)) register_1 (.D(WData), .en(and_9_out), .Q(register_1_q), .clk(and_17_out), .clr(Reset));
  Register #(.width(16)) register_2 (.D(WData), .en(and_10_out), .Q(register_2_q), .clk(and_17_out), .clr(Reset));
  Register #(.width(16)) register_3 (.D(WData), .en(and_11_out), .Q(register_3_q), .clk(and_17_out), .clr(Reset));
  Register #(.width(16)) register_4 (.D(WData), .en(and_12_out), .Q(register_4_q), .clk(and_17_out), .clr(Reset));
  Register #(.width(16)) register_5 (.D(WData), .en(and_13_out), .Q(register_5_q), .clk(and_17_out), .clr(Reset));
  Register #(.width(16)) register_6 (.D(WData), .en(and_14_out), .Q(register_6_q), .clk(and_17_out), .clr(Reset));
  Register #(.width(16)) register_7 (.D(WData), .en(and_15_out), .Q(register_7_q), .clk(and_17_out), .clr(Reset));
  Register #(.width(16)) register_8 (.D(WData), .en(and_16_out), .Q(register_8_q), .clk(and_17_out), .clr(Reset));
  Multiplexer #(.select(3), .width(16)) multiplexer_1 (
    .in0(register_1_q), .in1(register_2_q), .in2(register_3_q), .in3(register_4_q), .in4(register_5_q),
    .in5(register_6_q), .in6(register_7_q), .in7(register_8_q), .out(A_Bus), .sel(ASel));  // open: en
  Multiplexer #(.select(3), .width(16)) multiplexer_2 (
    .in0(register_1_q), .in1(register_2_q), .in2(register_3_q), .in3(register_4_q), .in4(register_5_q),
    .in5(register_6_q), .in6(register_7_q), .in7(register_8_q), .out(B_Bus), .sel(BSel));  // open: en
  Multiplexer #(.select(3), .width(16)) multiplexer_3 (
    .in0(register_1_q), .in1(register_2_q), .in2(register_3_q), .in3(register_4_q), .in4(register_5_q),
    .in5(register_6_q), .in6(register_7_q), .in7(register_8_q), .out(W_Bus), .sel(WSel));  // open: en

  // Notes on the sheet:
  //   using logical AND and OR to determine which registers to use
  //   ASel, BSel, etc are 3 bits (1-8 choices)
  //   WSel needs to select which specific register to update
  //   split up wsel, use those 3 bits in an and gate, and put in an and gate with WEn
endmodule

module Branch_Control_Unit (
  input  [2:0] BranchType,
  input  [3:0] CondCodes,
  output PCSel
);

  wire _0_out, _1_out, _1F_out, _2_2_out, _2_3_out, _2_4_out, _2_out, _2F_out, _3_2_out, _3_out, _3F_out,
       _4_out, _4F_out, _5_out, _5F_out, _6_out, _6F_out, _7_out, not_1_out, not_2_out, not_3_out, not_4_out;

  and _0 (_0_out, ~BranchType[0], ~BranchType[1], ~BranchType[2]);  // AND_Gate
  and _1 (_1_out, BranchType[0], ~BranchType[1], ~BranchType[2]);  // AND_Gate
  and _2 (_2_out, ~BranchType[0], BranchType[1], ~BranchType[2]);  // AND_Gate
  and _3 (_3_out, BranchType[0], BranchType[1], ~BranchType[2]);  // AND_Gate
  and _4 (_4_out, ~BranchType[0], ~BranchType[1], BranchType[2]);  // AND_Gate
  and _5 (_5_out, BranchType[0], ~BranchType[1], BranchType[2]);  // AND_Gate
  and _6 (_6_out, ~BranchType[0], BranchType[1], BranchType[2]);  // AND_Gate
  and _7 (_7_out, BranchType[0], BranchType[1], BranchType[2]);
  and _1F (_1F_out, _1_out, CondCodes[0]);
  and _2_2 (_2_2_out, CondCodes[2], CondCodes[3]);
  not not_1 (not_1_out, _2_3_out);
  or _2_3 (_2_3_out, CondCodes[2], CondCodes[3]);
  not not_2 (not_2_out, CondCodes[0]);
  and _2F (_2F_out, _2_out, _2_4_out);
  or _2_4 (_2_4_out, _2_2_out, not_1_out);
  and _3_2 (_3_2_out, _2_4_out, not_2_out);
  not not_3 (not_3_out, _2_4_out);
  not not_4 (not_4_out, _3_2_out);
  and _3F (_3F_out, _3_2_out, _3_out);
  and _4F (_4F_out, not_4_out, _4_out);
  and _5F (_5F_out, not_3_out, _5_out);
  and _6F (_6F_out, not_2_out, _6_out);
  Multiplexer #(.select(3)) multiplexer_1 (
    .in0(_0_out), .in1(_1F_out), .in2(_2F_out), .in3(_3F_out), .in4(_4F_out), .in5(_5F_out), .in6(_6F_out),
    .in7(_7_out), .out(PCSel), .sel(BranchType));  // open: en

  // Notes on the sheet:
  //   Look at RTN for all branches
  //   0 = b and call; 1 = b.eq; 2 = b.ge; 3 = b.gt; 4 = b.le; 5 = b.lt; 6 = b.ne; 7 = br and halt
endmodule

module _16_bit_counter (
  input  Clock,
  input  Reset,
  output [15:0] NextPC
);

  wire [15:0] bit_extender_1_out, n16_bit_ripple_adder_1_sum;

  assign bit_extender_1_out = {{15{1'b0}}, 1'b1};  // Bit_Extender bit_extender_1
  _16_bit_Ripple_Adder u_16_bit_ripple_adder_1 (
    .A(bit_extender_1_out), .B(NextPC), .CarryIn(1'b0), .Sum(n16_bit_ripple_adder_1_sum));  // open: CarryOut
  Register #(.width(16), .trigger("falling")) register_1 (
    .D(n16_bit_ripple_adder_1_sum), .Q(NextPC), .clk(Clock), .clr(Reset));  // open: en
endmodule

module _16_bit_Ripple_Adder (
  input  CarryIn,
  input  [15:0] A,
  input  [15:0] B,
  output [15:0] Sum,
  output CarryOut
);

  wire n3_2_adder_1_carryout, n3_2_adder_2_carryout, n3_2_adder_3_carryout, n3_2_adder_4_carryout,
       n3_2_adder_5_carryout, n3_2_adder_6_carryout, n3_2_adder_7_carryout, n3_2_adder_8_carryout,
       n3_2_adder_9_carryout, n3_2_adder_10_carryout, n3_2_adder_11_carryout, n3_2_adder_12_carryout,
       n3_2_adder_13_carryout, n3_2_adder_14_carryout, n3_2_adder_15_carryout;

  _3_2_Adder u_3_2_adder_1 (.A(A[0]), .B(B[0]), .CarryIn(CarryIn), .CarryOut(n3_2_adder_1_carryout), .Sum(Sum[0]));
  _3_2_Adder u_3_2_adder_2 (
    .A(A[1]), .B(B[1]), .CarryIn(n3_2_adder_1_carryout), .CarryOut(n3_2_adder_2_carryout), .Sum(Sum[1]));
  _3_2_Adder u_3_2_adder_3 (
    .A(A[2]), .B(B[2]), .CarryIn(n3_2_adder_2_carryout), .CarryOut(n3_2_adder_3_carryout), .Sum(Sum[2]));
  _3_2_Adder u_3_2_adder_4 (
    .A(A[3]), .B(B[3]), .CarryIn(n3_2_adder_3_carryout), .CarryOut(n3_2_adder_4_carryout), .Sum(Sum[3]));
  _3_2_Adder u_3_2_adder_5 (
    .A(A[4]), .B(B[4]), .CarryIn(n3_2_adder_4_carryout), .CarryOut(n3_2_adder_5_carryout), .Sum(Sum[4]));
  _3_2_Adder u_3_2_adder_6 (
    .A(A[5]), .B(B[5]), .CarryIn(n3_2_adder_5_carryout), .CarryOut(n3_2_adder_6_carryout), .Sum(Sum[5]));
  _3_2_Adder u_3_2_adder_7 (
    .A(A[6]), .B(B[6]), .CarryIn(n3_2_adder_6_carryout), .CarryOut(n3_2_adder_7_carryout), .Sum(Sum[6]));
  _3_2_Adder u_3_2_adder_8 (
    .A(A[7]), .B(B[7]), .CarryIn(n3_2_adder_7_carryout), .CarryOut(n3_2_adder_8_carryout), .Sum(Sum[7]));
  _3_2_Adder u_3_2_adder_9 (
    .A(A[8]), .B(B[8]), .CarryIn(n3_2_adder_8_carryout), .CarryOut(n3_2_adder_9_carryout), .Sum(Sum[8]));
  _3_2_Adder u_3_2_adder_10 (
    .A(A[9]), .B(B[9]), .CarryIn(n3_2_adder_9_carryout), .CarryOut(n3_2_adder_10_carryout), .Sum(Sum[9]));
  _3_2_Adder u_3_2_adder_11 (
    .A(A[10]), .B(B[10]), .CarryIn(n3_2_adder_10_carryout), .CarryOut(n3_2_adder_11_carryout), .Sum(Sum[10]));
  _3_2_Adder u_3_2_adder_12 (
    .A(A[11]), .B(B[11]), .CarryIn(n3_2_adder_11_carryout), .CarryOut(n3_2_adder_12_carryout), .Sum(Sum[11]));
  _3_2_Adder u_3_2_adder_13 (
    .A(A[12]), .B(B[12]), .CarryIn(n3_2_adder_12_carryout), .CarryOut(n3_2_adder_13_carryout), .Sum(Sum[12]));
  _3_2_Adder u_3_2_adder_14 (
    .A(A[13]), .B(B[13]), .CarryIn(n3_2_adder_13_carryout), .CarryOut(n3_2_adder_14_carryout), .Sum(Sum[13]));
  _3_2_Adder u_3_2_adder_15 (
    .A(A[14]), .B(B[14]), .CarryIn(n3_2_adder_14_carryout), .CarryOut(n3_2_adder_15_carryout), .Sum(Sum[14]));
  _3_2_Adder u_3_2_adder_16 (
    .A(A[15]), .B(B[15]), .CarryIn(n3_2_adder_15_carryout), .CarryOut(CarryOut), .Sum(Sum[15]));
endmodule
